# Fritzing sketch GPIO layoout diagram (saved by Fritzing 0.9.3b)
breadboards: 1

parts:
  S1 = Pushbutton [package="[THT]"]
  LED1 = Super Flux LED blue [color=Blue]
  LED2 = Super Flux LED blue [color=Blue]
  LED3 = Super Flux LED blue [color=Blue]
  LED4 = Super Flux LED blue [color=Blue]
  LED5 = Super Flux LED blue [color=Blue]
  LED6 = Super Flux LED blue [color=Blue]
  LED7 = Super Flux LED blue [color=Blue]
  LED8 = Super Flux LED blue [color=Blue]
  LED9 = Super Flux LED blue [color=Blue]
  LED10 = Super Flux LED blue [color=Blue]
  R1 = Resistor [tolerance=±5% resistance=220 package=THT]
  R2 = Resistor [tolerance=±5% resistance=220 package=THT]
  R3 = Resistor [tolerance=±5% resistance=220 package=THT]
  R4 = Resistor [tolerance=±5% resistance=220 package=THT]
  R5 = Resistor [tolerance=±5% resistance=220 package=THT]
  R6 = Resistor [tolerance=±5% resistance=220 package=THT]
  R7 = Resistor [tolerance=±5% resistance=220 package=THT]
  R8 = Resistor [tolerance=±5% resistance=220 package=THT]
  R9 = Resistor [tolerance=±5% resistance=220 package=THT]
  R10 = Resistor [tolerance=±5% resistance=220 package=THT]
  Raspberry_Pi_1 = Raspberry Pi 3 [part_number=RPI-3-V1.2]
  Sensore_PIR_HC-SR502 = HC-SR501 Body Sensor Module
  CAMERA3 = TTL Serial JPEG Camera  # not connected

nets:
  N1: S1.Pin_1, S1.Pin_2, R1.Pin_1, R3.Pin_1, R4.Pin_1, R5.Pin_1, R8.Pin_1
  N2: S1.Pin_3, S1.Pin_4, Raspberry_Pi_1.GPIO25
  N3: LED1.anode, R3.Pin_0
  N4: LED1.cathode, Raspberry_Pi_1.GPIO19
  N5: LED2.anode, R1.Pin_0
  N6: LED2.cathode, Raspberry_Pi_1.GPIO18
  N7: LED3.anode, R5.Pin_0
  N8: LED3.cathode, Raspberry_Pi_1.GPIO20
  N9: LED4.anode, R4.Pin_0
  N10: LED4.cathode, Raspberry_Pi_1.GPIO21
  N11: LED5.anode, R8.Pin_0
  N12: LED5.cathode, Raspberry_Pi_1.GPIO22
  N13: LED6.anode, R2.Pin_1
  N14: LED6.cathode, Raspberry_Pi_1.GPIO5, Raspberry_Pi_1.GND
  N15: LED7.anode, R9.Pin_1
  N16: LED7.cathode, Raspberry_Pi_1.GPIO16
  N17: LED8.anode, R10.Pin_1
  N18: LED8.cathode, Raspberry_Pi_1.GPIO23
  N19: LED9.anode, R6.Pin_1
  N20: LED9.cathode, Raspberry_Pi_1.GPIO12
  N21: LED10.anode, R7.Pin_1
  N22: LED10.cathode, Raspberry_Pi_1.GPIO6
  N23: R2.Pin_0, R6.Pin_0, R7.Pin_0, R9.Pin_0, R10.Pin_0, Sensore_PIR_HC-SR502.GND
  N24: Raspberry_Pi_1.GPIO26, Sensore_PIR_HC-SR502.OUT

custom parts:
  HC-SR501 Body Sensor Module: Pyroelectric Infrared PIR Motion Sensor Detector Module
  TTL Serial JPEG Camera: TTL Serial JPEG Camera with NTSC Out
